// Logisim project Logisim - Basic Computer.circ as structural Verilog: 20 circuits, main circuit ALU
module ALU (
  input  [15:0] DR,
  input  [15:0] AC,
  input  [2:0] selection_lines,
  output [15:0] \output ,
  output to_E
);

  wire [15:0] adder_1_out, and_1_out, not_1_out, shifter_1_out, shifter_2_out;

  assign and_1_out = DR & AC;  // AND_Gate and_1, 16 bits wide
  Adder #(.width(16)) adder_1 (.a(DR), .b(AC), .out(adder_1_out), .cin(1'b0), .cout(to_E));
  assign not_1_out = ~AC;  // NOT_Gate not_1, 16 bits wide
  Shifter #(.width(16), .shift("lr")) shifter_1 (.in(AC), .\dist (4'b0001), .out(shifter_1_out));
  Shifter #(.width(16)) shifter_2 (.in(AC), .\dist (4'b0001), .out(shifter_2_out));
  Multiplexer #(.select(3), .width(16)) multiplexer_1 (
    .in0(and_1_out), .in1(adder_1_out), .in2(DR), .in3(not_1_out), .in4(shifter_1_out), .in5(shifter_2_out),
    .out(\output ), .sel(selection_lines), .en(1'b1));  // open: in6, in7
endmodule

module Computer (
  input  INR,
  input  CLR,
  input  CLR_2,
  input  load,
  input  INR_2,
  input  CLR_3,
  output E
);

  wire AC_CLR, ac_clr_1_clr_ac, AC_INC, AC_LD, ALU_to_e, and_1_out, AR_LD, B0, B2, B5, B9, B11, clock_out,
       D1, D2, D3, D4, D5, D6, D7, d_ff_4_q, DR_INC, DR_LD, I, LD_PC, MemoryRead, MemoryWrite, not_1_out,
       PC_INC, R, S, SC_CLR, sc_clr_1_clr_sc, T0, T1, T2, T3, T4, T5, T6, x1, x2, x3, x4;
  wire [2:0] alu_selection_1_alu_selection, priority_encoder_1_out;
  wire [10:1] control_unit_p12;
  wire [11:0] AR_q, bit_extender_1_out, bit_extender_2_out, PC_q;
  wire [15:0] AC_out, ALU_output, bit_extender_3_out, bit_extender_4_out, DR_out, IR_q, multiplexer_1_out,
       ram_1_data, TR_q;

  R r_1 (.D7(D7), .I(I), .T3(T3), .out_4(R));
  AC_CLR ac_clr_1 (.r(R), .B11(B11), .CLR_AC(ac_clr_1_clr_ac));
  SC_CLR sc_clr_1 (
    .D2(D2), .T5(T5), .D4(D4), .T4(T4), .D3(D3), .T4_2(T4), .D1(D1), .T5_2(T5), .D6(D6), .T6(T6),
    .CLR_SC(sc_clr_1_clr_sc));
  DR_INC dr_inc_1 (.D6(D6), .T5(T5), .INC_DR(DR_INC));
  DR_LD dr_ld_1 (.D2(D2), .T4(T4), .D1(D1), .T4_2(T4), .D6(D6), .T4_3(T4), .LD_DR(DR_LD));
  AC_INC ac_inc_1 (.r(R), .B5(B5), .INC_AC(AC_INC));
  AC_LD ac_ld_1 (.D2(D2), .T5(T5), .r(R), .B9(B9), .D1(D1), .T5_2(T5), .LD_AC(AC_LD));
  PC_LD pc_ld_1 (.D4(D4), .T4(T4), .LD_PC(LD_PC));
  MemoryWrite memorywrite_1 (.D3(D3), .T4(T4), .D6(D6), .T6(T6), .Write(MemoryWrite));
  x2_PC x2_pc_1 (.R(R), .T0(T0), .x2(x2));
  D_Flip_Flop d_ff_1 (.clk(clock_out), .D(ac_clr_1_clr_ac), .Q(AC_CLR));  // open: Qn, preset, en, reset
  D_Flip_Flop d_ff_2 (.clk(clock_out), .D(sc_clr_1_clr_sc), .Q(SC_CLR));  // open: Qn, preset, en, reset
  MemoryRead memoryread_1 (
    .D2(D2), .T4(T4), .D1(D1), .T4_2(T4), .D6(D6), .T4_3(T4), .T1(T1), .I(I), .D7(D7), .T3(T3),
    .MemoryRead(MemoryRead));
  x1_AR x1_ar_1 (.D4(D4), .T4(T4), .x1__AR(x1));
  x3 x3_1 (.D2(D2), .T5(T5), .D6(D6), .T6(T6), .x3(x3));
  x4_AC x4_ac_1 (.D3(D3), .T4(T4), .x4__AC(x4));
  PC_INC pc_inc_1 (.zero_AC(AC_out), .B2(B2), .R(R), .T1(T1), .zero_DR(DR_out), .D6(D6), .T6(T6), .PC_INC(PC_INC));
  AR_LD ar_ld_1 (.T0(T2), .T2(T0), .I(I), .D7(D7), .T3(T3), .LD_AR(AR_LD));
  ALU_Selection alu_selection_1 (
    .D1(D1), .T5(T5), .D2(D2), .T5_2(T5), .r(R), .B9(B9), .ALU_Selection(alu_selection_1_alu_selection));  // open: AND, CIR, CIL
  D_Flip_Flop d_ff_3 (.clk(clock_out), .D(ALU_to_e), .Q(E), .en(1'b1));  // open: Qn, preset, reset
  Bit_Extender #(.in_width(16), .out_width(12)) bit_extender_1 (.in(multiplexer_1_out), .out(bit_extender_1_out));
  Bit_Extender #(.in_width(16), .out_width(12)) bit_extender_2 (.in(multiplexer_1_out), .out(bit_extender_2_out));
  ALU ALU (
    .DR(DR_out), .AC(AC_out), .to_E(ALU_to_e), .selection_lines(alu_selection_1_alu_selection),
    .\output (ALU_output));
  Clock clock (.out(clock_out));
  Counter #(.width(12), .max('hfff)) AR (
    .load(AR_LD), .D(bit_extender_1_out), .count(INR), .Q(AR_q), .clk(clock_out), .clr(d_ff_4_q));  // open: carry
  Counter #(.width(12), .max('hfff)) PC (
    .load(LD_PC), .D(bit_extender_2_out), .count(PC_INC), .Q(PC_q), .clk(clock_out), .clr(CLR));  // open: carry
  Counter #(.width(16), .max('hffff)) DR (
    .load(DR_LD), .D(multiplexer_1_out), .count(DR_INC), .Q(DR_out), .clk(clock_out), .clr(CLR_2));  // open: carry
  Counter #(.width(16), .max('hffff)) AC (
    .load(AC_LD), .D(ALU_output), .count(AC_INC), .Q(AC_out), .clk(clock_out), .clr(AC_CLR));  // open: carry
  Counter #(.width(16), .max('hffff)) IR (
    .load(T1), .D(multiplexer_1_out), .count(1'b0), .Q(IR_q), .clk(clock_out), .clr(1'b0));  // open: carry
  Counter #(.width(16), .max('hffff)) TR (
    .load(load), .D(multiplexer_1_out), .count(INR_2), .Q(TR_q), .clk(clock_out), .clr(CLR_3));  // open: carry
  RAM #(.addrWidth(12), .dataWidth(16), .bus("separate")) ram_1 (
    .addr(AR_q), .din(multiplexer_1_out), .data(ram_1_data), .str(MemoryWrite), .clk(clock_out),
    .ld(MemoryRead));  // open: sel, clr
  assign bit_extender_3_out = {{4{1'b0}}, AR_q};  // Bit_Extender bit_extender_3
  D_Flip_Flop d_ff_4 (.clk(clock_out), .D(AC_CLR), .Q(d_ff_4_q));  // open: Qn, preset, en, reset
  assign bit_extender_4_out = {{4{1'b0}}, PC_q};  // Bit_Extender bit_extender_4
  Multiplexer #(.select(3), .width(16)) multiplexer_1 (
    .in1(bit_extender_3_out), .in2(bit_extender_4_out), .in3(DR_out), .in4(AC_out), .in5(IR_q), .in6(TR_q),
    .in7(ram_1_data), .out(multiplexer_1_out), .sel(priority_encoder_1_out), .en(1'b1));  // open: in0
  Priority_Encoder priority_encoder_1 (
    .in0(1'b0), .in1(x1), .in2(x2), .in3(x3), .in4(x4), .in5(T2), .in6(1'b0), .in7(MemoryRead),
    .out(priority_encoder_1_out), .en_in(1'b1));
  // Control_Unit control_unit: pin names not known; wires that end beside it: S, D1, D2, D3, D4, D5, D6, D7, IR_q, SC_CLR, clock_out, {B11, control_unit_p12[10], B9, control_unit_p12[8:6], B5, control_unit_p12[4:3], B2, control_unit_p12[1], B0}, I, T0, T1, T2, T3, T4, T5, T6
  D_Flip_Flop u_S (.clk(clock_out), .D(1'b1), .Q(S), .en(not_1_out));  // open: Qn, preset, reset
  not not_1 (not_1_out, and_1_out);
  and and_1 (and_1_out, R, B0);
endmodule

module Control_Unit (
  input  [15:0] IR,
  input  S,
  input  CLR_SC,
  output T0,
  output T1,
  output [11:0] IR_0_11,
  output T2,
  output T3,
  output T4,
  output D0,
  output T5,
  output D1,
  output T6,
  output D2,
  output T7,
  output D3,
  output T8,
  output D4,
  output T9,
  output D5,
  output T10,
  output D6,
  output T11,
  output D7,
  output T12,
  output T13,
  output T14,
  output I,
  output T15
);

  wire clock_1_out;
  wire [3:0] SC_q;

  Counter #(.width(4), .max('hf)) SC (.count(S), .Q(SC_q), .clk(clock_1_out), .clr(CLR_SC));  // open: load, D, carry
  Decoder #(.select(4)) decoder_1 (
    .out0(T0), .out1(T1), .out2(T2), .out3(T3), .out4(T4), .out5(T5), .out6(T6), .out7(T7), .out8(T8),
    .out9(T9), .out10(T10), .out11(T11), .out12(T12), .out13(T13), .out14(T14), .out15(T15), .sel(SC_q),
    .en(1'b1));
  Clock clock_1 (.out(clock_1_out));
  D_Flip_Flop d_ff_1 (.clk(clock_1_out), .D(IR[15]), .Q(I), .en(1'b1));  // open: Qn, preset, reset
  Decoder #(.select(3)) decoder_2 (
    .out0(D0), .out1(D1), .out2(D2), .out3(D3), .out4(D4), .out5(D5), .out6(D6), .out7(D7), .sel(IR[14:12]),
    .en(1'b1));

  assign IR_0_11 = IR[11:0];
endmodule

module AC_CLR (
  input  r,
  input  B11,
  output CLR_AC
);

  and and_1 (CLR_AC, r, B11);
endmodule

module SC_CLR (
  input  D2,
  input  T5,
  input  D4,
  input  T4,
  input  D3,
  input  T4_2,
  input  D1,
  input  T5_2,
  input  D6,
  input  T6,
  output CLR_SC
);

  wire and_1_out, and_2_out, and_3_out, and_4_out, and_5_out;

  and and_1 (and_1_out, D2, T5);
  and and_2 (and_2_out, D4, T4);
  and and_3 (and_3_out, D3, T4_2);
  and and_4 (and_4_out, D1, T5_2);
  and and_5 (and_5_out, D6, T6);
  or or_1 (CLR_SC, and_1_out, and_2_out, and_3_out, and_4_out, and_5_out);
endmodule

module DR_INC (
  input  D6,
  input  T5,
  output INC_DR
);

  and and_1 (INC_DR, D6, T5);
endmodule

module DR_LD (
  input  D2,
  input  T4,
  input  D1,
  input  T4_2,
  input  D6,
  input  T4_3,
  output LD_DR
);

  wire and_1_out, and_2_out, and_3_out;

  and and_1 (and_1_out, D2, T4);
  and and_2 (and_2_out, D1, T4_2);
  and and_3 (and_3_out, D6, T4_3);
  or or_1 (LD_DR, and_1_out, and_2_out, and_3_out);
endmodule

module AC_INC (
  input  r,
  input  B5,
  output INC_AC
);

  and and_1 (INC_AC, r, B5);
endmodule

module AC_LD (
  input  D2,
  input  T5,
  input  r,
  input  B9,
  input  D1,
  input  T5_2,
  output LD_AC
);

  wire and_1_out, and_2_out, and_3_out;

  and and_1 (and_1_out, D2, T5);
  and and_2 (and_2_out, r, B9);
  and and_3 (and_3_out, D1, T5_2);
  or or_1 (LD_AC, and_1_out, and_2_out, and_3_out);
endmodule

module PC_LD (
  input  D4,
  input  T4,
  output LD_PC
);

  and and_1 (LD_PC, D4, T4);
endmodule

module MemoryRead (
  input  D2,
  input  T4,
  input  D1,
  input  T4_2,
  input  D6,
  input  T4_3,
  input  T1,
  input  I,
  input  D7,
  input  T3,
  output MemoryRead
);

  wire and_1_out, and_2_out, and_3_out, and_4_out, not_1_out;

  and and_1 (and_1_out, D2, T4);
  and and_2 (and_2_out, D1, T4_2);
  and and_3 (and_3_out, D6, T4_3);
  not not_1 (not_1_out, D7);
  and and_4 (and_4_out, I, not_1_out, T3);
  or or_1 (MemoryRead, and_1_out, and_2_out, and_4_out, T1, and_3_out);
endmodule

module MemoryWrite (
  input  D3,
  input  T4,
  input  D6,
  input  T6,
  output Write
);

  wire and_1_out, and_2_out;

  and and_1 (and_1_out, D3, T4);
  and and_2 (and_2_out, D6, T6);
  or or_1 (Write, and_1_out, and_2_out);
endmodule

module x1_AR (
  input  D4,
  input  T4,
  output x1__AR
);

  and and_1 (x1__AR, D4, T4);
endmodule

module x3 (
  input  D2,
  input  T5,
  input  D6,
  input  T6,
  output x3
);

  wire and_1_out, and_2_out;

  and and_1 (and_1_out, D2, T5);
  and and_2 (and_2_out, D6, T6);
  or or_1 (x3, and_1_out, and_2_out);
endmodule

module x4_AC (
  input  D3,
  input  T4,
  output x4__AC
);

  and and_1 (x4__AC, D3, T4);
endmodule

module R (
  input  D7,
  input  I,
  input  T3,
  output out_4
);

  wire not_1_out;

  not not_1 (not_1_out, I);
  and and_1 (out_4, D7, not_1_out, T3);
endmodule

module PC_INC (
  input  [15:0] zero_AC,
  input  B2,
  input  R,
  input  T1,
  input  [15:0] zero_DR,
  input  D6,
  input  T6,
  output PC_INC
);

  wire and_1_out, and_2_out, nor_1_out, nor_2_out;

  nor nor_1 (nor_1_out, zero_AC[0], zero_AC[1], zero_AC[2], zero_AC[3], zero_AC[4], zero_AC[5], zero_AC[6], zero_AC[7], zero_AC[8], zero_AC[9], zero_AC[10], zero_AC[11], zero_AC[12], zero_AC[13], zero_AC[14], zero_AC[15]);
  nor nor_2 (nor_2_out, zero_DR[0], zero_DR[1], zero_DR[2], zero_DR[3], zero_DR[4], zero_DR[5], zero_DR[6], zero_DR[7], zero_DR[8], zero_DR[9], zero_DR[10], zero_DR[11], zero_DR[12], zero_DR[13], zero_DR[14], zero_DR[15]);
  and and_1 (and_1_out, nor_1_out, B2, R);
  and and_2 (and_2_out, nor_2_out, D6, T6);
  or or_1 (PC_INC, and_1_out, T1, and_2_out);
endmodule

module ALU_Selection (
  input  D1,
  input  T5,
  input  AND,
  input  D2,
  input  T5_2,
  input  CIR,
  input  CIL,
  input  r,
  input  B9,
  output [2:0] ALU_Selection
);

  wire and_2_out, and_3_out, CMA;

  and and_1 (CMA, r, B9);
  and and_2 (and_2_out, D2, T5_2);
  and and_3 (and_3_out, D1, T5);
  Priority_Encoder priority_encoder_1 (
    .in0(AND), .in1(and_3_out), .in2(and_2_out), .in3(CMA), .in4(CIR), .in5(CIL), .in6(1'b0), .in7(1'b0),
    .out(ALU_Selection), .en_in(1'b1));  // open: gs, en_out
endmodule

module AR_LD (
  input  T0,
  input  T2,
  input  I,
  input  D7,
  input  T3,
  output LD_AR
);

  wire and_1_out, not_1_out;

  not not_1 (not_1_out, D7);
  and and_1 (and_1_out, I, not_1_out, T3);
  or or_1 (LD_AR, T0, T2, and_1_out);
endmodule

module x2_PC (
  input  R,
  input  T0,
  output x2
);

  wire not_1_out;

  not not_1 (not_1_out, R);
  and and_1 (x2, not_1_out, T0);
endmodule
